# Fritzing sketch servo-robot-kol (saved by Fritzing 0.9.3b)
breadboards: 1

parts:
  Part1 = Arduino Uno (Rev3) - ICSP
  J2 = Basic Servo
  J1 = Basic Servo
  Part2 = Thumb Joystick

nets:
  N1: Part1.A1, Part2.HORZ
  N2: Part1.A2, Part2.VERT
  N3: Part1.D9_PWM, J1.pulse
  N4: Part1.D10_PWM/SS, J2.pulse
